# Fritzing sketch grizzlyGuide (saved by Fritzing 0.9.3b)

parts:
  Part1 = Arduino Uno (Rev3)
  Arduino_CNC_Shield_V3_00_1 = Arduino_CNC_V3.00
  Part2 = Arduino Uno (Rev3)
  M3 = Stepper Motor - Bipolar
  Part3 = LCD1602-I2C
  Part4 = 4x4 Keypad [part_number=101207]
  JL012-13-5_1 = JL012-13-5.2 Lever (Limit) Switch SPDT + NO + NC [part_number=JL012-13-5.2]
  JL012-13-5_2 = JL012-13-5.2 Lever (Limit) Switch SPDT + NO + NC [part_number=JL012-13-5.2]
  M4 = Stepper Motor - Bipolar
  PS1 = prefix0000 [part_number=S-350-60]

nets:
  N1: Part1.A4/SDA, Part2.A4/SDA, Part3.SDA
  N2: Part1.A5/SCL, Part2.A5/SCL, Part3.SCL
  N3: Arduino_CNC_Shield_V3_00_1.POWER_-, PS1.connector3
  N4: Arduino_CNC_Shield_V3_00_1.POWER_+, PS1.connector0
  N5: Arduino_CNC_Shield_V3_00_1.X-MTR_'1', M4.C
  N6: Arduino_CNC_Shield_V3_00_1.X-MTR_'2', M4.D
  N7: Arduino_CNC_Shield_V3_00_1.X-MTR_'3', M4.B
  N8: Arduino_CNC_Shield_V3_00_1.X-MTR_'4', M4.A
  N9: Arduino_CNC_Shield_V3_00_1.Y-MTR_'1', M3.C
  N10: Arduino_CNC_Shield_V3_00_1.Y-MTR_'2', M3.D
  N11: Arduino_CNC_Shield_V3_00_1.Y-MTR_'3', M3.B
  N12: Arduino_CNC_Shield_V3_00_1.Y-MTR_'4', M3.A
  N13: Arduino_CNC_Shield_V3_00_1.End_Stops_Y+_(and_Y-), JL012-13-5_2.C
  N14: Arduino_CNC_Shield_V3_00_1.End_Stops_Y+_(Gnd), JL012-13-5_2.NO
  N15: Arduino_CNC_Shield_V3_00_1.End_Stops_X+_(and_X-), JL012-13-5_1.C
  N16: Arduino_CNC_Shield_V3_00_1.End_Stops_X+_(Gnd), JL012-13-5_1.NO
  N17: Part2.D8, Part4.2
  N18: Part2.D9_PWM, Part4.1
  N19: Part2.D2, Part4.8
  N20: Part2.D3_PWM, Part4.7
  N21: Part2.D4, Part4.6
  N22: Part2.D5_PWM, Part4.5
  N23: Part2.D6_PWM, Part4.4
  N24: Part2.D7, Part4.3
  5V: Part2.5V, Part3.VCC
  GND: Part2.GND, Part3.GND

custom parts:
  Arduino_CNC_V3.00: Protoneer Arduino CNC Shield V3.00 If using Grbl V0.9: The “A” axis can not be used (yet). The “SCL” (Arduino A5) pin is now used for 'Probing' input. The “End Stops Z+ & Z-” (Arduino D11) and “SpnEn” (Arduino D12) have been switched!
  LCD1602-I2C: A standard character display, usually with 2x16 characters. Comes in many colors with LCM1602 IIC attached.
  4x4 Keypad: Matrix membrane keypad 4x4
  JL012-13-5.2 Lever (Limit) Switch SPDT + NO + NC: Micro Switch; Model No.: JL012-13.5-2; Actuator Action: Momentary; Actuator Type: Hinge Lever; Contact Configuration: 1NO, 1NC (SPDT) Temperature -25~65℃；Relative humidity: below 85%; Rate Voltage: 125V AC; Rated Current: 1A.
